# Fritzing sketch PrototypeV1 (saved by Fritzing 1.0.6)
breadboards: 1

parts:
  R1 = Resistor [tolerance=±5% resistance=10k package="0402 [SMD]"]
  R3 = Resistor [tolerance=±5% resistance=10k package="0402 [SMD]"]
  uPesy_ESP32_Wroom_DevKit1 = uPesy ESP32 Wroom DevKit v2
  R2 = Resistor [tolerance=±5% resistance=1k package="0402 [SMD]"]
  R4 = Resistor [tolerance=±5% resistance=10k package="0402 [SMD]"]
  R5 = Resistor [tolerance=±5% resistance=1k package="0402 [SMD]"]
  R6 = Resistor [tolerance=±5% resistance=10k package="0402 [SMD]"]
  Adafruit_BNO055_and_BMP280_BFF1 = Adafruit BNO055 and BMP280 BFF [mn=Adafruit mpn=#5937 part_number=#5937]
  Part1 = TRRS 3.5mm Jack Breakout  # not connected
  Part2 = TRRS 3.5mm Jack Breakout  # not connected
  U1 = LM358 [package=dip08]

nets:
  N1: R1.Pin_0, R3.Pin_1, R2.Pin_0
  N2: R1.Pin_1, uPesy_ESP32_Wroom_DevKit1.GND#16, R6.Pin_1, Adafruit_BNO055_and_BMP280_BFF1.GND, U1.G$1_V-
  N3: R3.Pin_0, uPesy_ESP32_Wroom_DevKit1.GPIO25
  N4: uPesy_ESP32_Wroom_DevKit1.GPIO22, Adafruit_BNO055_and_BMP280_BFF1.SCL
  N5: uPesy_ESP32_Wroom_DevKit1.GPIO21, Adafruit_BNO055_and_BMP280_BFF1.SDA
  3V3: uPesy_ESP32_Wroom_DevKit1.3V3, Adafruit_BNO055_and_BMP280_BFF1.3.3V
  N6: uPesy_ESP32_Wroom_DevKit1.5V, U1.G$1_V+
  N7: uPesy_ESP32_Wroom_DevKit1.GPIO26, R4.Pin_0
  N8: R2.Pin_1, U1.G$1_+IN
  N9: R4.Pin_1, R5.Pin_0, R6.Pin_0
  N10: R5.Pin_1, U1.G$2_+IN
  N11: U1.G$1_OUT, U1.G$1_-IN
  N12: U1.G$2_-IN, U1.G$2_OUT

custom parts:
  uPesy ESP32 Wroom DevKit v2: ESP32 development board that is 100% breadboard compatible
